# Fritzing sketch fritzing_sketch_master (saved by Fritzing 0.9.2b)
perfboards: 1

parts:
  Part1 = Arduino Pro Mini v13
  Part2 = RFID-RC522-v2
  LED1 = DUO LED RG [package="5 mm [THT]"]
  R1 = Resistor [tolerance=±5% resistance=300 package=THT]
  U1 = Voltage Regulator [package=to220-adj]
  R2 = Resistor [tolerance=±5% resistance=390 package=THT]
  Power_plug1 = Power plug
  R3 = Resistor [tolerance=±5% resistance=220 package=THT]

nets:
  N1: Part1.VCC, LED1.red_anode
  N2: Part1.D13/SCK, Part2.SCK
  N3: Part1.D12/MISO, Part2.MISO
  N4: Part1.D11_PWM/MOSI, Part2.MOSI
  N5: Part1.D10_PWM/SS, Part2.SDA
  N6: Part1.D9_PWM, Part2.RST
  GND: Part2.GND, R2.Pin_1, Power_plug1.GND
  N7: Part2.3.3V, U1.OUT, R3.Pin_0
  N8: LED1.common_cathode, R1.Pin_0
  N9: U1.ADJ, R2.Pin_0, R3.Pin_1
  N10: U1.IN, Power_plug1.VCC

custom parts:
  RFID-RC522-v2: A simple China made RFID-RC522 Reader; do check the pin labels, as this is a MFRC522 based clone.
